// Logisim project Processador.circ as structural Verilog: 12 circuits, main circuit Banco_de_Registradores
module Main (
  output [31:0] out_1
);

  wire and_1_out, B_OU_C, Clock_Main, DISPLAY_EN, MUX_IP, MUX_IP_COND, or_1_out, ula_1_zero, WE_IP, WE_REG;
  wire [2:0] mem_controle_1_op;
  wire [3:0] Op;
  wire [27:0] rom_1_data;
  wire [31:0] banco_de_registradores_1_a, banco_de_registradores_1_b, extsig_1_out_2, extunsig_1_out_2,
       multiplexer_1_out, multiplexer_2_out, registrador_32bits_1_q, somador32_1_q, ula_1_saida;

  Clock clock_1 (.out(Clock_Main));
  and and_1 (and_1_out, MUX_IP_COND, ula_1_zero);
  or or_1 (or_1_out, and_1_out, MUX_IP);
  Multiplexer #(.width(32)) multiplexer_1 (.in0(32'h1), .in1(extsig_1_out_2), .out(multiplexer_1_out), .sel(or_1_out));
  Somador32 somador32_1 (.A(registrador_32bits_1_q), .B(multiplexer_1_out), .CIN(1'b0), .Q(somador32_1_q));
  ROM #(.addrWidth(24), .dataWidth(32)) rom_1 (.addr(registrador_32bits_1_q[23:0]), .data({Op, rom_1_data}));
  Registrador_32Bits registrador_32bits_1 (
    .D(somador32_1_q), .WE(WE_IP), .Clock(Clock_Main), .Q(registrador_32bits_1_q));
  EXTSIG extsig_1 (.in_1(rom_1_data[15:0]), .out_2(extsig_1_out_2));
  Banco_de_Registradores banco_de_registradores_1 (
    .C(ula_1_saida), .R_a(rom_1_data[27:24]), .R_b(rom_1_data[23:20]), .R_c(rom_1_data[19:16]),
    .Write_Enable(WE_REG), .Clock_R(Clock_Main), .A(banco_de_registradores_1_a),
    .B(banco_de_registradores_1_b));
  EXTUNSIG extunsig_1 (.in_1(rom_1_data[15:0]), .out_2(extunsig_1_out_2));
  Mem_controle mem_controle_1 (
    .in_1(Op), .Op(mem_controle_1_op), .WE_REG(WE_REG), .Mux_IP(MUX_IP), .B_ou_C(B_OU_C),
    .Display(DISPLAY_EN), .Mux_IP_Condicional(MUX_IP_COND), .WE_IP(WE_IP));
  Multiplexer #(.width(32)) multiplexer_2 (
    .in0(banco_de_registradores_1_b), .in1(extunsig_1_out_2), .out(multiplexer_2_out), .sel(B_OU_C));
  Display display_1 (.Entrada(banco_de_registradores_1_a), .Enable(DISPLAY_EN), .Clock(Clock_Main), .Saida(out_1));
  ULA ula_1 (
    .A(banco_de_registradores_1_a), .B(multiplexer_2_out), .Funcao(mem_controle_1_op), .Zero(ula_1_zero),
    .Saida(ula_1_saida));
  // also tied to GND on the sheet: {registrador_32bits_1_q[24], registrador_32bits_1_q[25], registrador_32bits_1_q[26], registrador_32bits_1_q[27], registrador_32bits_1_q[28], registrador_32bits_1_q[29], registrador_32bits_1_q[30], registrador_32bits_1_q[31]}

  // Notes on the sheet:
  //   contents of rom_1 (hex, n*v repeats v):
  //   0 b001000f b0020003 11230000 c3000000 21230000 c3000000 31230000 c3000000 41230000 c3000000 51230000
  //   c3000000 61230000 c3000000 71230000 c3000000 81230000 c3000000 91230000 c3000000 a1230000 c3000000
  //   d0000003 b202000c c2000000 e120000c f0000000
endmodule

module Banco_de_Registradores (
  input  [31:0] C,
  input  [3:0] R_a,
  input  [3:0] R_b,
  input  [3:0] R_c,
  input  Write_Enable,
  input  Clock_R,
  output [31:0] A,
  output [31:0] B
);

  wire demultiplexer_1_out0, WE_1, WE_2, WE_3, WE_4, WE_5, WE_6, WE_7, WE_8, WE_9, WE_10, WE_11, WE_12,
       WE_13, WE_14, WE_15;
  wire [31:0] Reg_0, Reg_1, Reg_2, Reg_3, Reg_4, Reg_5, Reg_6, Reg_7, Reg_8, Reg_9, Reg_10, Reg_11, Reg_12,
       Reg_13, Reg_14, Reg_15;

  Demultiplexer #(.select(4)) demultiplexer_1 (
    .out0(demultiplexer_1_out0), .out1(WE_1), .out2(WE_2), .out3(WE_3), .out4(WE_4), .out5(WE_5),
    .out6(WE_6), .out7(WE_7), .out8(WE_8), .out9(WE_9), .out10(WE_10), .out11(WE_11), .out12(WE_12),
    .out13(WE_13), .out14(WE_14), .out15(WE_15), .in(Write_Enable), .sel(R_c));
  Registrador_32Bits registrador_32bits_1 (.D(C), .WE(1'b0), .Clock(Clock_R), .Q(Reg_0));
  Registrador_32Bits registrador_32bits_2 (.D(C), .WE(WE_1), .Clock(Clock_R), .Q(Reg_1));
  Registrador_32Bits registrador_32bits_3 (.D(C), .WE(WE_2), .Clock(Clock_R), .Q(Reg_2));
  Registrador_32Bits registrador_32bits_4 (.D(C), .WE(WE_3), .Clock(Clock_R), .Q(Reg_3));
  Registrador_32Bits registrador_32bits_5 (.D(C), .WE(WE_4), .Clock(Clock_R), .Q(Reg_4));
  Registrador_32Bits registrador_32bits_6 (.D(C), .WE(WE_5), .Clock(Clock_R), .Q(Reg_5));
  Registrador_32Bits registrador_32bits_7 (.D(C), .WE(WE_6), .Clock(Clock_R), .Q(Reg_6));
  Registrador_32Bits registrador_32bits_8 (.D(C), .WE(WE_7), .Clock(Clock_R), .Q(Reg_7));
  Registrador_32Bits registrador_32bits_9 (.D(C), .WE(WE_8), .Clock(Clock_R), .Q(Reg_8));
  Registrador_32Bits registrador_32bits_10 (.D(C), .WE(WE_9), .Clock(Clock_R), .Q(Reg_9));
  Registrador_32Bits registrador_32bits_11 (.D(C), .WE(WE_10), .Clock(Clock_R), .Q(Reg_10));
  Registrador_32Bits registrador_32bits_12 (.D(C), .WE(WE_11), .Clock(Clock_R), .Q(Reg_11));
  Registrador_32Bits registrador_32bits_13 (.D(C), .WE(WE_12), .Clock(Clock_R), .Q(Reg_12));
  Registrador_32Bits registrador_32bits_14 (.D(C), .WE(WE_13), .Clock(Clock_R), .Q(Reg_13));
  Registrador_32Bits registrador_32bits_15 (.D(C), .WE(WE_14), .Clock(Clock_R), .Q(Reg_14));
  Registrador_32Bits registrador_32bits_16 (.D(C), .WE(WE_15), .Clock(Clock_R), .Q(Reg_15));
  Multiplexer #(.select(4), .width(32)) multiplexer_1 (
    .in0(Reg_0), .in1(Reg_1), .in2(Reg_2), .in3(Reg_3), .in4(Reg_4), .in5(Reg_5), .in6(Reg_6), .in7(Reg_7),
    .in8(Reg_8), .in9(Reg_9), .in10(Reg_10), .in11(Reg_11), .in12(Reg_12), .in13(Reg_13), .in14(Reg_14),
    .in15(Reg_15), .out(A), .sel(R_a));
  Multiplexer #(.select(4), .width(32)) multiplexer_2 (
    .in0(Reg_0), .in1(Reg_1), .in2(Reg_2), .in3(Reg_3), .in4(Reg_4), .in5(Reg_5), .in6(Reg_6), .in7(Reg_7),
    .in8(Reg_8), .in9(Reg_9), .in10(Reg_10), .in11(Reg_11), .in12(Reg_12), .in13(Reg_13), .in14(Reg_14),
    .in15(Reg_15), .out(B), .sel(R_b));
  // also tied to GND on the sheet: demultiplexer_1_out0
endmodule

module ULA (
  input  [31:0] A,
  input  [31:0] B,
  input  [2:0] Funcao,
  output Zero,
  output [31:0] Saida
);

  wire nor_1_out, nor_2_out;
  wire [31:0] and_1_out, not_1_out, not_2_out, or_1_out, shift_dir_1_saida, shifter_esq_1_saida,
       somador32_1_q, somador32_2_q, xor_1_out;

  assign not_1_out = ~B;  // NOT_Gate not_1, 32 bits wide
  assign and_1_out = A & B;  // AND_Gate and_1, 32 bits wide
  assign or_1_out = A | B;  // OR_Gate or_1, 32 bits wide
  assign xor_1_out = A ^ B;  // XOR_Gate xor_1, 32 bits wide
  assign not_2_out = ~A;  // NOT_Gate not_2, 32 bits wide
  Somador32 somador32_1 (.A(A), .B(B), .CIN(1'b0), .Q(somador32_1_q));
  Somador32 somador32_2 (.A(A), .B(not_1_out), .CIN(1'b1), .Q(somador32_2_q));
  Shifter_Esq shifter_esq_1 (.ENTRADA(A), .Quant(B), .Saida(shifter_esq_1_saida));
  Shift_Dir shift_dir_1 (.ENTRADA(A), .Quant(B), .Saida(shift_dir_1_saida));
  Multiplexer #(.select(3), .width(32)) multiplexer_1 (
    .in0(somador32_1_q), .in1(somador32_2_q), .in2(and_1_out), .in3(or_1_out), .in4(xor_1_out),
    .in5(not_2_out), .in6(shifter_esq_1_saida), .in7(shift_dir_1_saida), .out(Saida), .sel(Funcao));
  nor nor_1 (nor_1_out, Saida[0], Saida[1], Saida[2], Saida[3], Saida[4], Saida[5], Saida[6], Saida[7], Saida[8], Saida[9], Saida[10], Saida[11], Saida[12], Saida[13], Saida[14]);
  nor nor_2 (nor_2_out, Saida[15], Saida[16], Saida[17], Saida[18], Saida[19], Saida[20], Saida[21], Saida[22], Saida[23], Saida[24], Saida[25], Saida[26], Saida[27], Saida[28], Saida[29], Saida[30], Saida[31]);
  and and_2 (Zero, nor_1_out, nor_2_out);
endmodule

module Shifter_Esq (
  input  [31:0] ENTRADA,
  input  [31:0] Quant,
  output [31:0] Saida
);

  wire Maior_que_31, or_1_out, or_2_out;
  wire [31:0] multiplexer_1_out, multiplexer_2_out, multiplexer_3_out, multiplexer_5_out;
  wire [31:16] multiplexer_4_out, multiplexer_4_out_2;

  or or_1 (or_1_out, Quant[31], Quant[30], Quant[29], Quant[28], Quant[27], Quant[26], Quant[25], Quant[24], Quant[23], Quant[22], Quant[21], Quant[20], Quant[19], Quant[18], Quant[17]);
  or or_2 (or_2_out, Quant[16], Quant[15], Quant[14], Quant[13], Quant[12], Quant[11], Quant[10], Quant[9], Quant[8], Quant[7], Quant[6]);
  or or_3 (Maior_que_31, or_1_out, or_2_out, Quant[5]);
  Multiplexer #(.width(32)) multiplexer_1 (
    .in0(ENTRADA), .in1({ENTRADA[30:0], 1'b0}), .out(multiplexer_1_out), .sel(Quant[0]));
  Multiplexer #(.width(32)) multiplexer_2 (
    .in0(multiplexer_1_out), .in1({multiplexer_1_out[29:0], 2'b00}), .out(multiplexer_2_out), .sel(Quant[1]));
  Multiplexer #(.width(32)) multiplexer_3 (
    .in0(multiplexer_2_out), .in1({multiplexer_2_out[27:0], 4'b0000}), .out(multiplexer_3_out), .sel(Quant[2]));
  Multiplexer #(.width(32)) multiplexer_4 (
    .in0(multiplexer_3_out), .in1({multiplexer_3_out[23:0], {8{1'b0}}}),
    .out({multiplexer_4_out, multiplexer_4_out_2}), .sel(Quant[3]));
  Multiplexer #(.width(32)) multiplexer_5 (
    .in0({multiplexer_4_out, multiplexer_4_out_2}), .in1({multiplexer_4_out_2, {16{1'b0}}}),
    .out(multiplexer_5_out), .sel(Quant[4]));
  Multiplexer #(.width(32)) multiplexer_6 (.in0(multiplexer_5_out), .in1({32{1'b0}}), .out(Saida), .sel(Maior_que_31));
endmodule

module Shift_Dir (
  input  [31:0] ENTRADA,
  input  [31:0] Quant,
  output [31:0] Saida
);

  wire Maior_que_31, or_1_out, or_2_out;
  wire [15:0] multiplexer_4_out, multiplexer_4_out_2;
  wire [31:0] multiplexer_1_out, multiplexer_2_out, multiplexer_3_out, multiplexer_5_out;

  or or_1 (or_1_out, Quant[31], Quant[30], Quant[29], Quant[28], Quant[27], Quant[26], Quant[25], Quant[24], Quant[23], Quant[22], Quant[21], Quant[20], Quant[19], Quant[18], Quant[17]);
  or or_2 (or_2_out, Quant[16], Quant[15], Quant[14], Quant[13], Quant[12], Quant[11], Quant[10], Quant[9], Quant[8], Quant[7], Quant[6]);
  or or_3 (Maior_que_31, or_1_out, or_2_out, Quant[5]);
  Multiplexer #(.width(32)) multiplexer_1 (
    .in0(ENTRADA), .in1({1'b0, ENTRADA[31:1]}), .out(multiplexer_1_out), .sel(Quant[0]));
  Multiplexer #(.width(32)) multiplexer_2 (
    .in0(multiplexer_1_out), .in1({2'b00, multiplexer_1_out[31:2]}), .out(multiplexer_2_out), .sel(Quant[1]));
  Multiplexer #(.width(32)) multiplexer_3 (
    .in0(multiplexer_2_out), .in1({4'b0000, multiplexer_2_out[31:4]}), .out(multiplexer_3_out), .sel(Quant[2]));
  Multiplexer #(.width(32)) multiplexer_4 (
    .in0(multiplexer_3_out), .in1({{8{1'b0}}, multiplexer_3_out[31:8]}),
    .out({multiplexer_4_out_2, multiplexer_4_out}), .sel(Quant[3]));
  Multiplexer #(.width(32)) multiplexer_5 (
    .in0({multiplexer_4_out_2, multiplexer_4_out}), .in1({{16{1'b0}}, multiplexer_4_out_2}),
    .out(multiplexer_5_out), .sel(Quant[4]));
  Multiplexer #(.width(32)) multiplexer_6 (.in0(multiplexer_5_out), .in1({32{1'b0}}), .out(Saida), .sel(Maior_que_31));
endmodule

module Registrador_32Bits (
  input  [31:0] D,
  input  WE,
  input  Clock,
  output [31:0] Q
);

  wire multiplexer_1_out, multiplexer_2_out, multiplexer_3_out, multiplexer_4_out, multiplexer_5_out,
       multiplexer_6_out, multiplexer_7_out, multiplexer_8_out, multiplexer_9_out, multiplexer_10_out,
       multiplexer_11_out, multiplexer_12_out, multiplexer_13_out, multiplexer_14_out, multiplexer_15_out,
       multiplexer_16_out, multiplexer_17_out, multiplexer_18_out, multiplexer_19_out, multiplexer_20_out,
       multiplexer_21_out, multiplexer_22_out, multiplexer_23_out, multiplexer_24_out, multiplexer_25_out,
       multiplexer_26_out, multiplexer_27_out, multiplexer_28_out, multiplexer_29_out, multiplexer_30_out,
       multiplexer_31_out, multiplexer_32_out;

  D_Flip_Flop d_ff_1 (.D(multiplexer_1_out), .clk(Clock), .Q(Q[0]));  // open: Qn, preset, reset
  Multiplexer multiplexer_1 (.in0(Q[0]), .in1(D[0]), .out(multiplexer_1_out), .sel(WE));
  D_Flip_Flop d_ff_2 (.D(multiplexer_2_out), .clk(Clock), .Q(Q[1]));  // open: Qn, preset, reset
  Multiplexer multiplexer_2 (.in0(Q[1]), .in1(D[1]), .out(multiplexer_2_out), .sel(WE));
  D_Flip_Flop d_ff_3 (.D(multiplexer_3_out), .clk(Clock), .Q(Q[2]));  // open: Qn, preset, reset
  Multiplexer multiplexer_3 (.in0(Q[2]), .in1(D[2]), .out(multiplexer_3_out), .sel(WE));
  D_Flip_Flop d_ff_4 (.D(multiplexer_4_out), .clk(Clock), .Q(Q[3]));  // open: Qn, preset, reset
  Multiplexer multiplexer_4 (.in0(Q[3]), .in1(D[3]), .out(multiplexer_4_out), .sel(WE));
  D_Flip_Flop d_ff_5 (.D(multiplexer_5_out), .clk(Clock), .Q(Q[4]));  // open: Qn, preset, reset
  Multiplexer multiplexer_5 (.in0(Q[4]), .in1(D[4]), .out(multiplexer_5_out), .sel(WE));
  D_Flip_Flop d_ff_6 (.D(multiplexer_6_out), .clk(Clock), .Q(Q[5]));  // open: Qn, preset, reset
  Multiplexer multiplexer_6 (.in0(Q[5]), .in1(D[5]), .out(multiplexer_6_out), .sel(WE));
  D_Flip_Flop d_ff_7 (.D(multiplexer_7_out), .clk(Clock), .Q(Q[6]));  // open: Qn, preset, reset
  Multiplexer multiplexer_7 (.in0(Q[6]), .in1(D[6]), .out(multiplexer_7_out), .sel(WE));
  D_Flip_Flop d_ff_8 (.D(multiplexer_8_out), .clk(Clock), .Q(Q[7]));  // open: Qn, preset, reset
  Multiplexer multiplexer_8 (.in0(Q[7]), .in1(D[7]), .out(multiplexer_8_out), .sel(WE));
  Multiplexer multiplexer_9 (.in0(Q[8]), .in1(D[8]), .out(multiplexer_9_out), .sel(WE));
  Multiplexer multiplexer_10 (.in0(Q[9]), .in1(D[9]), .out(multiplexer_10_out), .sel(WE));
  Multiplexer multiplexer_11 (.in0(Q[10]), .in1(D[10]), .out(multiplexer_11_out), .sel(WE));
  Multiplexer multiplexer_12 (.in0(Q[11]), .in1(D[11]), .out(multiplexer_12_out), .sel(WE));
  Multiplexer multiplexer_13 (.in0(Q[12]), .in1(D[12]), .out(multiplexer_13_out), .sel(WE));
  Multiplexer multiplexer_14 (.in0(Q[13]), .in1(D[13]), .out(multiplexer_14_out), .sel(WE));
  Multiplexer multiplexer_15 (.in0(Q[14]), .in1(D[14]), .out(multiplexer_15_out), .sel(WE));
  Multiplexer multiplexer_16 (.in0(Q[15]), .in1(D[15]), .out(multiplexer_16_out), .sel(WE));
  D_Flip_Flop d_ff_9 (.D(multiplexer_9_out), .clk(Clock), .Q(Q[8]));  // open: Qn, preset, reset
  D_Flip_Flop d_ff_10 (.D(multiplexer_10_out), .clk(Clock), .Q(Q[9]));  // open: Qn, preset, reset
  D_Flip_Flop d_ff_11 (.D(multiplexer_11_out), .clk(Clock), .Q(Q[10]));  // open: Qn, preset, reset
  D_Flip_Flop d_ff_12 (.D(multiplexer_12_out), .clk(Clock), .Q(Q[11]));  // open: Qn, preset, reset
  D_Flip_Flop d_ff_13 (.D(multiplexer_13_out), .clk(Clock), .Q(Q[12]));  // open: Qn, preset, reset
  D_Flip_Flop d_ff_14 (.D(multiplexer_14_out), .clk(Clock), .Q(Q[13]));  // open: Qn, preset, reset
  D_Flip_Flop d_ff_15 (.D(multiplexer_15_out), .clk(Clock), .Q(Q[14]));  // open: Qn, preset, reset
  D_Flip_Flop d_ff_16 (.D(multiplexer_16_out), .clk(Clock), .Q(Q[15]));  // open: Qn, preset, reset
  Multiplexer multiplexer_17 (.in0(Q[16]), .in1(D[16]), .out(multiplexer_17_out), .sel(WE));
  Multiplexer multiplexer_18 (.in0(Q[17]), .in1(D[17]), .out(multiplexer_18_out), .sel(WE));
  Multiplexer multiplexer_19 (.in0(Q[18]), .in1(D[18]), .out(multiplexer_19_out), .sel(WE));
  Multiplexer multiplexer_20 (.in0(Q[19]), .in1(D[19]), .out(multiplexer_20_out), .sel(WE));
  Multiplexer multiplexer_21 (.in0(Q[20]), .in1(D[20]), .out(multiplexer_21_out), .sel(WE));
  Multiplexer multiplexer_22 (.in0(Q[21]), .in1(D[21]), .out(multiplexer_22_out), .sel(WE));
  Multiplexer multiplexer_23 (.in0(Q[22]), .in1(D[22]), .out(multiplexer_23_out), .sel(WE));
  Multiplexer multiplexer_24 (.in0(Q[23]), .in1(D[23]), .out(multiplexer_24_out), .sel(WE));
  D_Flip_Flop d_ff_17 (.D(multiplexer_17_out), .clk(Clock), .Q(Q[16]));  // open: Qn, preset, reset
  D_Flip_Flop d_ff_18 (.D(multiplexer_18_out), .clk(Clock), .Q(Q[17]));  // open: Qn, preset, reset
  D_Flip_Flop d_ff_19 (.D(multiplexer_19_out), .clk(Clock), .Q(Q[18]));  // open: Qn, preset, reset
  D_Flip_Flop d_ff_20 (.D(multiplexer_20_out), .clk(Clock), .Q(Q[19]));  // open: Qn, preset, reset
  D_Flip_Flop d_ff_21 (.D(multiplexer_21_out), .clk(Clock), .Q(Q[20]));  // open: Qn, preset, reset
  D_Flip_Flop d_ff_22 (.D(multiplexer_22_out), .clk(Clock), .Q(Q[21]));  // open: Qn, preset, reset
  D_Flip_Flop d_ff_23 (.D(multiplexer_23_out), .clk(Clock), .Q(Q[22]));  // open: Qn, preset, reset
  D_Flip_Flop d_ff_24 (.D(multiplexer_24_out), .clk(Clock), .Q(Q[23]));  // open: Qn, preset, reset
  Multiplexer multiplexer_25 (.in0(Q[24]), .in1(D[24]), .out(multiplexer_25_out), .sel(WE));
  Multiplexer multiplexer_26 (.in0(Q[25]), .in1(D[25]), .out(multiplexer_26_out), .sel(WE));
  Multiplexer multiplexer_27 (.in0(Q[26]), .in1(D[26]), .out(multiplexer_27_out), .sel(WE));
  Multiplexer multiplexer_28 (.in0(Q[27]), .in1(D[27]), .out(multiplexer_28_out), .sel(WE));
  Multiplexer multiplexer_29 (.in0(Q[28]), .in1(D[28]), .out(multiplexer_29_out), .sel(WE));
  Multiplexer multiplexer_30 (.in0(Q[29]), .in1(D[29]), .out(multiplexer_30_out), .sel(WE));
  Multiplexer multiplexer_31 (.in0(Q[30]), .in1(D[30]), .out(multiplexer_31_out), .sel(WE));
  Multiplexer multiplexer_32 (.in0(Q[31]), .in1(D[31]), .out(multiplexer_32_out), .sel(WE));
  D_Flip_Flop d_ff_25 (.D(multiplexer_25_out), .clk(Clock), .Q(Q[24]));  // open: Qn, preset, reset
  D_Flip_Flop d_ff_26 (.D(multiplexer_26_out), .clk(Clock), .Q(Q[25]));  // open: Qn, preset, reset
  D_Flip_Flop d_ff_27 (.D(multiplexer_27_out), .clk(Clock), .Q(Q[26]));  // open: Qn, preset, reset
  D_Flip_Flop d_ff_28 (.D(multiplexer_28_out), .clk(Clock), .Q(Q[27]));  // open: Qn, preset, reset
  D_Flip_Flop d_ff_29 (.D(multiplexer_29_out), .clk(Clock), .Q(Q[28]));  // open: Qn, preset, reset
  D_Flip_Flop d_ff_30 (.D(multiplexer_30_out), .clk(Clock), .Q(Q[29]));  // open: Qn, preset, reset
  D_Flip_Flop d_ff_31 (.D(multiplexer_31_out), .clk(Clock), .Q(Q[30]));  // open: Qn, preset, reset
  D_Flip_Flop d_ff_32 (.D(multiplexer_32_out), .clk(Clock), .Q(Q[31]));  // open: Qn, preset, reset
endmodule

module Somador32 (
  input  [31:0] A,
  input  [31:0] B,
  input  CIN,
  output [31:0] Q
);

  wire cla4bit_1_cout, cla4bit_2_cout, cla4bit_3_cout, cla4bit_4_cout, cla4bit_5_cout, cla4bit_6_cout,
       cla4bit_7_cout, cla4bit_8_cout;

  CLA4bit cla4bit_1 (
    .A3(A[3]), .A2(A[2]), .A1(A[1]), .A0(A[0]), .B3(B[3]), .B2(B[2]), .B1(B[1]), .B0(B[0]), .CIN(CIN),
    .SUM0(Q[0]), .SUM1(Q[1]), .SUM2(Q[2]), .SUM3(Q[3]), .COUT(cla4bit_1_cout));
  CLA4bit cla4bit_2 (
    .A3(A[7]), .A2(A[6]), .A1(A[5]), .A0(A[4]), .B3(B[7]), .B2(B[6]), .B1(B[5]), .B0(B[4]),
    .CIN(cla4bit_1_cout), .SUM0(Q[4]), .SUM1(Q[5]), .SUM2(Q[6]), .SUM3(Q[7]), .COUT(cla4bit_2_cout));
  CLA4bit cla4bit_3 (
    .A3(A[11]), .A2(A[10]), .A1(A[9]), .A0(A[8]), .B3(B[11]), .B2(B[10]), .B1(B[9]), .B0(B[8]),
    .CIN(cla4bit_2_cout), .SUM0(Q[8]), .SUM1(Q[9]), .SUM2(Q[10]), .SUM3(Q[11]), .COUT(cla4bit_3_cout));
  CLA4bit cla4bit_4 (
    .A3(A[15]), .A2(A[14]), .A1(A[13]), .A0(A[12]), .B3(B[15]), .B2(B[14]), .B1(B[13]), .B0(B[12]),
    .CIN(cla4bit_3_cout), .SUM0(Q[12]), .SUM1(Q[13]), .SUM2(Q[14]), .SUM3(Q[15]), .COUT(cla4bit_4_cout));
  CLA4bit cla4bit_5 (
    .A3(A[19]), .A2(A[18]), .A1(A[17]), .A0(A[16]), .B3(B[19]), .B2(B[18]), .B1(B[17]), .B0(B[16]),
    .CIN(cla4bit_4_cout), .SUM0(Q[16]), .SUM1(Q[17]), .SUM2(Q[18]), .SUM3(Q[19]), .COUT(cla4bit_5_cout));
  CLA4bit cla4bit_6 (
    .A3(A[23]), .A2(A[22]), .A1(A[21]), .A0(A[20]), .B3(B[23]), .B2(B[22]), .B1(B[21]), .B0(B[20]),
    .CIN(cla4bit_5_cout), .SUM0(Q[20]), .SUM1(Q[21]), .SUM2(Q[22]), .SUM3(Q[23]), .COUT(cla4bit_6_cout));
  CLA4bit cla4bit_7 (
    .A3(A[27]), .A2(A[26]), .A1(A[25]), .A0(A[24]), .B3(B[27]), .B2(B[26]), .B1(B[25]), .B0(B[24]),
    .CIN(cla4bit_6_cout), .SUM0(Q[24]), .SUM1(Q[25]), .SUM2(Q[26]), .SUM3(Q[27]), .COUT(cla4bit_7_cout));
  CLA4bit cla4bit_8 (
    .A3(A[31]), .A2(A[30]), .A1(A[29]), .A0(A[28]), .B3(B[31]), .B2(B[30]), .B1(B[29]), .B0(B[28]),
    .CIN(cla4bit_7_cout), .SUM0(Q[28]), .SUM1(Q[29]), .SUM2(Q[30]), .SUM3(Q[31]), .COUT(cla4bit_8_cout));
  // NoConnect on cla4bit_8_cout
endmodule

module CLA4bit (
  input  A3,
  input  A2,
  input  A1,
  input  A0,
  input  B3,
  input  B2,
  input  B1,
  input  B0,
  input  CIN,
  output SUM0,
  output SUM1,
  output SUM2,
  output SUM3,
  output COUT
);

  wire and_1_out, and_2_out, and_3_out, and_4_out, and_5_out, G0, G1, G2, or_1_out, or_2_out, or_4_out,
       or_5_out, or_6_out, or_7_out, or_8_out, or_9_out, or_10_out, or_11_out, or_12_out, or_13_out,
       or_14_out, P0C0, P1GO, P1P0C0, P2G1, P2P1GO, P2P1P0C0, xor_1_out, xor_3_out, xor_5_out, xor_7_out;

  or or_1 (or_1_out, A3, B3);
  xor xor_1 (xor_1_out, A3, B3);
  and and_1 (and_1_out, P2P1P0C0, or_1_out);
  or or_2 (or_2_out, and_1_out, and_2_out);
  and and_2 (and_2_out, or_1_out, G2);
  or or_3 (COUT, or_2_out, or_5_out);
  xor xor_2 (SUM3, xor_1_out, or_8_out);
  and and_3 (and_3_out, P2P1GO, or_1_out);
  and and_4 (and_4_out, P2G1, or_1_out);
  or or_4 (or_4_out, and_3_out, and_4_out);
  and and_5 (and_5_out, A3, B3);
  or or_5 (or_5_out, or_4_out, and_5_out);
  xor xor_3 (xor_3_out, A2, B2);
  xor xor_4 (SUM2, xor_3_out, or_11_out);
  or or_6 (or_6_out, A2, B2);
  and and_6 (P2P1GO, P1GO, or_6_out);
  or or_7 (or_7_out, P2P1GO, P2G1);
  and and_7 (G2, A2, B2);
  and and_8 (P2P1P0C0, or_6_out, P1P0C0);
  and and_9 (P2G1, or_6_out, G1);
  or or_8 (or_8_out, or_7_out, or_9_out);
  or or_9 (or_9_out, P2P1P0C0, G2);
  xor xor_5 (xor_5_out, A1, B1);
  or or_10 (or_10_out, A1, B1);
  and and_10 (P1GO, G0, or_10_out);
  xor xor_6 (SUM1, xor_5_out, or_14_out);
  or or_11 (or_11_out, P1GO, or_12_out);
  and and_11 (G1, A1, B1);
  and and_12 (P1P0C0, or_10_out, P0C0);
  or or_12 (or_12_out, P1P0C0, G1);
  xor xor_7 (xor_7_out, A0, B0);
  or or_13 (or_13_out, A0, B0);
  and and_13 (P0C0, CIN, or_13_out);
  xor xor_8 (SUM0, xor_7_out, CIN);
  and and_14 (G0, A0, B0);
  or or_14 (or_14_out, P0C0, G0);
endmodule

module Display (
  input  [31:0] Entrada,
  input  Enable,
  input  Clock,
  output [31:0] Saida
);

  Registrador_32Bits registrador_32bits_1 (.D(Entrada), .WE(Enable), .Clock(Clock), .Q(Saida));
endmodule

module Mem_controle (
  input  [3:0] in_1,
  output [2:0] Op,
  output WE_REG,
  output Mux_IP,
  output B_ou_C,
  output Display,
  output Mux_IP_Condicional,
  output WE_IP
);

  ROM #(.addrWidth(4), .dataWidth(9)) rom_1 (
    .addr(in_1), .data({Op, WE_REG, Mux_IP, B_ou_C, Display, Mux_IP_Condicional, WE_IP}));

  // Notes on the sheet:
  //   contents of rom_1 (hex, n*v repeats v):
  //   1 21 61 a1 e1 121 161 1a1 1e1 e9 129 29 5 11 43
endmodule

module EXTSIG (
  input  [15:0] in_1,
  output [31:0] out_2
);


  assign out_2 = {{17{in_1[15]}}, in_1[14:0]};
endmodule

module EXTUNSIG (
  input  [15:0] in_1,
  output [31:0] out_2
);


  assign out_2 = {{16{1'b0}}, in_1};
endmodule
